# Fritzing sketch Schematic (saved by Fritzing 0.9.3b)
breadboards: 3

parts:
  SG3 = Buzzer 12mm [package=buzzer-12mm-ns]  # not connected
  Part2 = Arduino Uno (Rev3) - ICSP  # not connected
  LED1 = LEDs [package=led10mm]
  R1 = Resistor [tolerance=±5% resistance=220 package="0603 [SMD]"]
  Part3 = Arduino Uno (Rev3) - ICSP  # not connected
  SG4 = Buzzer 12mm [package=buzzer-12mm-ns]  # not connected
  Part4 = Arduino Uno (Rev3) - ICSP
  LED2 = LEDs [package=led10mm]
  R2 = Resistor [tolerance=±5% resistance=220 package="0603 [SMD]"]

nets:
  N1: LED1.C, LED1.A, R1.Pin_1
  N2: Part4.D2, R2.Pin_0
  N3: Part4.GND, LED2.C, LED2.A, R2.Pin_1
